// Logisim project Digital Clock.circ as structural Verilog: 5 circuits, main circuit main
module main (
  input  A,
  input  B,
  input  C,
  input  D,
  output out_5,
  output out_6,
  output out_7,
  output out_8,
  output g,
  output out_10,
  output out_11
);

  wire and_1_out, and_2_out, and_3_out, and_4_out, and_5_out, and_6_out, and_7_out, and_8_out, and_9_out,
       not_1_out, not_2_out, not_3_out, or_1_out, or_2_out, xnor_1_out, xnor_2_out;

  not not_1 (not_1_out, B);
  not not_2 (not_2_out, C);
  not not_3 (not_3_out, D);
  or or_1 (or_1_out, A, C);
  or or_2 (or_2_out, B, not_2_out);
  and and_1 (and_1_out, not_2_out, not_3_out);
  and and_2 (and_2_out, B, not_2_out);
  and and_3 (and_3_out, B, not_3_out);
  and and_4 (and_4_out, B, not_3_out);
  and and_5 (and_5_out, not_2_out, B);
  and and_6 (and_6_out, not_1_out, C);
  and and_7 (and_7_out, C, not_3_out);
  and and_8 (and_8_out, not_3_out, not_1_out);
  and and_9 (and_9_out, B, not_2_out, D);
  xnor xnor_1 (xnor_1_out, B, D);
  xnor xnor_2 (xnor_2_out, C, D);
  or or_3 (out_5, or_1_out, xnor_1_out);
  or or_4 (out_6, xnor_2_out, not_1_out);
  or or_5 (out_7, or_2_out, D);
  or or_6 (out_8, A, and_1_out, and_2_out, and_3_out);
  or or_7 (g, and_4_out, A, and_5_out, and_6_out);
  or or_8 (out_10, and_7_out, and_8_out);
  or or_9 (out_11, and_7_out, and_8_out, and_6_out, and_9_out, A);

  // Notes on the sheet:
  //   B'
  //   c'
  //   D'
  //   a
  //   b
  //   c
  //   f
  //   e
  //   d
endmodule

module counter (
  input  in_1,
  input  in_2,
  input  in_3,
  input  in_4
);

  wire main_1_g, main_1_out_5, main_1_out_6, main_1_out_7, main_1_out_8, main_1_out_10, main_1_out_11;

  main main_1 (
    .A(in_1), .B(in_2), .C(in_3), .D(in_4), .out_5(main_1_out_5), .out_6(main_1_out_6), .out_7(main_1_out_7),
    .out_8(main_1_out_8), .g(main_1_g), .out_10(main_1_out_10), .out_11(main_1_out_11));
  _7_Segment_Display u_7_segment_display_1 (
    .g(main_1_g), .f(main_1_out_8), .a(main_1_out_5), .b(main_1_out_6), .e(main_1_out_10), .d(main_1_out_11),
    .c(main_1_out_7));  // open: dp
endmodule

module ff (
  input  in_1,
  input  in_2,
  input  in_3,
  input  in_4,
  input  in_5,
  input  in_6
);

  wire and_1_out, and_2_out, and_3_out, and_4_out, and_5_out, clock_1_out, j_k_ff_1_q, j_k_ff_2_q,
       j_k_ff_3_q, j_k_ff_4_q, j_k_ff_5_q, j_k_ff_6_q, j_k_ff_7_q, j_k_ff_8_q, j_k_ff_9_q, j_k_ff_10_q,
       j_k_ff_11_q, j_k_ff_12_q, j_k_ff_13_q, j_k_ff_14_q, main_1_g, main_1_out_5, main_1_out_6,
       main_1_out_7, main_1_out_8, main_1_out_10, main_1_out_11, main_2_g, main_2_out_5, main_2_out_6,
       main_2_out_7, main_2_out_8, main_2_out_10, main_2_out_11, main_3_g, main_3_out_5, main_3_out_6,
       main_3_out_7, main_3_out_8, main_3_out_10, main_3_out_11, main_4_g, main_4_out_5, main_4_out_6,
       main_4_out_7, main_4_out_8, main_4_out_10, main_4_out_11, not_1_out, not_2_out, not_3_out, not_4_out,
       not_5_out, not_6_out, not_7_out;

  Clock clock_1 (.out(clock_1_out));
  not not_1 (not_1_out, j_k_ff_3_q);
  not not_2 (not_2_out, j_k_ff_2_q);
  and and_1 (and_1_out, not_2_out, j_k_ff_7_q, j_k_ff_10_q);
  and and_2 (and_2_out, j_k_ff_5_q, j_k_ff_8_q, j_k_ff_13_q, not_3_out);
  and and_3 (and_3_out, not_1_out, j_k_ff_6_q, j_k_ff_11_q);
  J_K_Flip_Flop #(.trigger("falling")) j_k_ff_1 (
    .J(in_3), .clk(and_1_out), .K(in_3), .Q(j_k_ff_1_q), .reset(and_4_out));  // open: Qn, preset, en
  J_K_Flip_Flop #(.trigger("falling")) j_k_ff_2 (
    .J(in_4), .clk(and_5_out), .K(in_4), .Q(j_k_ff_2_q), .reset(and_1_out));  // open: Qn, preset, en
  J_K_Flip_Flop #(.trigger("falling")) j_k_ff_3 (
    .J(in_1), .clk(and_4_out), .K(in_1), .Q(j_k_ff_3_q), .reset(and_3_out));  // open: Qn, preset, en
  not not_3 (not_3_out, j_k_ff_14_q);
  J_K_Flip_Flop #(.trigger("falling")) j_k_ff_4 (
    .J(in_3), .clk(j_k_ff_1_q), .K(in_3), .Q(j_k_ff_4_q), .reset(and_4_out));  // open: Qn, preset, en
  J_K_Flip_Flop #(.trigger("falling")) j_k_ff_5 (
    .J(in_6), .clk(clock_1_out), .K(in_6), .Q(j_k_ff_5_q), .reset(and_5_out));  // open: Qn, preset, en
  J_K_Flip_Flop #(.trigger("falling")) j_k_ff_6 (
    .J(in_1), .clk(j_k_ff_3_q), .K(in_1), .Q(j_k_ff_6_q), .reset(and_3_out));  // open: Qn, preset, en
  J_K_Flip_Flop #(.trigger("falling")) j_k_ff_7 (
    .J(in_4), .clk(j_k_ff_2_q), .K(in_4), .Q(j_k_ff_7_q), .reset(and_1_out));  // open: Qn, preset, en
  J_K_Flip_Flop #(.trigger("falling")) j_k_ff_8 (
    .J(in_6), .clk(j_k_ff_5_q), .K(in_6), .Q(j_k_ff_8_q), .reset(and_5_out));  // open: Qn, preset, en
  J_K_Flip_Flop #(.trigger("falling")) j_k_ff_9 (
    .J(in_3), .clk(j_k_ff_4_q), .K(in_3), .Q(j_k_ff_9_q), .reset(and_4_out));  // open: Qn, preset, en
  J_K_Flip_Flop #(.trigger("falling")) j_k_ff_10 (
    .J(in_4), .clk(j_k_ff_7_q), .K(in_4), .Q(j_k_ff_10_q), .reset(and_1_out));  // open: Qn, preset, en
  J_K_Flip_Flop #(.trigger("falling")) j_k_ff_11 (
    .J(in_1), .clk(j_k_ff_6_q), .K(in_1), .Q(j_k_ff_11_q), .reset(and_3_out));  // open: Qn, preset, en
  J_K_Flip_Flop #(.trigger("falling")) j_k_ff_12 (
    .J(in_3), .clk(j_k_ff_9_q), .K(in_3), .Q(j_k_ff_12_q), .reset(and_4_out));  // open: Qn, preset, en
  and and_4 (and_4_out, not_4_out, not_5_out, j_k_ff_4_q, j_k_ff_12_q);
  not not_4 (not_4_out, j_k_ff_9_q);
  not not_5 (not_5_out, j_k_ff_1_q);
  J_K_Flip_Flop #(.trigger("falling")) j_k_ff_13 (
    .J(in_6), .clk(j_k_ff_8_q), .K(in_6), .Q(j_k_ff_13_q), .reset(and_5_out));  // open: Qn, preset, en
  main main_1 (
    .A(j_k_ff_12_q), .B(j_k_ff_9_q), .C(j_k_ff_4_q), .D(j_k_ff_1_q), .out_5(main_1_out_5),
    .out_6(main_1_out_6), .out_7(main_1_out_7), .out_8(main_1_out_8), .g(main_1_g), .out_10(main_1_out_10),
    .out_11(main_1_out_11));
  main main_2 (
    .A(in_5), .B(j_k_ff_10_q), .C(j_k_ff_7_q), .D(j_k_ff_2_q), .out_5(main_2_out_5), .out_6(main_2_out_6),
    .out_7(main_2_out_7), .out_8(main_2_out_8), .g(main_2_g), .out_10(main_2_out_10), .out_11(main_2_out_11));
  J_K_Flip_Flop #(.trigger("falling")) j_k_ff_14 (
    .J(in_6), .clk(j_k_ff_13_q), .K(in_6), .Q(j_k_ff_14_q), .reset(and_5_out));  // open: Qn, preset, en
  and and_5 (and_5_out, not_6_out, not_7_out, j_k_ff_8_q, j_k_ff_14_q);
  main main_3 (
    .A(in_2), .B(j_k_ff_11_q), .C(j_k_ff_6_q), .D(j_k_ff_3_q), .out_5(main_3_out_5), .out_6(main_3_out_6),
    .out_7(main_3_out_7), .out_8(main_3_out_8), .g(main_3_g), .out_10(main_3_out_10), .out_11(main_3_out_11));
  not not_6 (not_6_out, j_k_ff_13_q);
  not not_7 (not_7_out, j_k_ff_5_q);
  main main_4 (
    .A(j_k_ff_14_q), .B(j_k_ff_13_q), .C(j_k_ff_8_q), .D(j_k_ff_5_q), .out_5(main_4_out_5),
    .out_6(main_4_out_6), .out_7(main_4_out_7), .out_8(main_4_out_8), .g(main_4_g), .out_10(main_4_out_10),
    .out_11(main_4_out_11));
  _7_Segment_Display u_7_segment_display_1 (
    .g(main_3_g), .f(main_3_out_8), .a(main_3_out_5), .b(main_3_out_6), .e(main_3_out_10), .d(main_3_out_11),
    .c(main_3_out_7));  // open: dp
  _7_Segment_Display u_7_segment_display_2 (
    .g(main_1_g), .f(main_1_out_8), .a(main_1_out_5), .b(main_1_out_6), .e(main_1_out_10), .d(main_1_out_11),
    .c(main_1_out_7));  // open: dp
  _7_Segment_Display u_7_segment_display_3 (
    .g(main_2_g), .f(main_2_out_8), .a(main_2_out_5), .b(main_2_out_6), .e(main_2_out_10), .d(main_2_out_11),
    .c(main_2_out_7));  // open: dp
  _7_Segment_Display u_7_segment_display_4 (
    .g(main_4_g), .f(main_4_out_8), .a(main_4_out_5), .b(main_4_out_6), .e(main_4_out_10), .d(main_4_out_11),
    .c(main_4_out_7));  // open: dp

  // Notes on the sheet:
  //   B
  //   B
  //   B
  //   C
  //   C
  //   C
  //   C
  //   D
  //   D
  //   D
  //   A
  //   D
  //   A
endmodule

module syncronus (
  input  in_1,
  input  in_2,
  input  in_3,
  input  in_4,
  input  in_5,
  input  in_6,
  input  in_7,
  input  in_8,
  input  in_9
);

  wire and_1_out, and_2_out, and_3_out, and_4_out, and_5_out, and_6_out, and_7_out, and_8_out, and_9_out,
       and_10_out, and_11_out, and_12_out, and_13_out, and_14_out, and_15_out, and_16_out, and_17_out,
       and_18_out, and_19_out, and_20_out, and_21_out, and_22_out, clock_1_out, main_1_g, main_1_out_5,
       main_1_out_6, main_1_out_7, main_1_out_8, main_1_out_10, main_1_out_11, main_2_g, main_2_out_5,
       main_2_out_6, main_2_out_7, main_2_out_8, main_2_out_10, main_2_out_11, main_3_g, main_3_out_5,
       main_3_out_6, main_3_out_7, main_3_out_8, main_3_out_10, main_3_out_11, main_4_g, main_4_out_5,
       main_4_out_6, main_4_out_7, main_4_out_8, main_4_out_10, main_4_out_11, main_5_g, main_5_out_5,
       main_5_out_6, main_5_out_7, main_5_out_8, main_5_out_10, main_5_out_11, main_6_g, main_6_out_5,
       main_6_out_6, main_6_out_7, main_6_out_8, main_6_out_10, main_6_out_11, not_1_out, not_2_out,
       not_3_out, not_4_out, not_5_out, not_6_out, not_7_out, not_8_out, not_9_out, not_10_out, not_11_out,
       not_12_out, not_13_out, not_14_out, not_15_out, not_16_out, not_17_out, not_18_out, not_19_out,
       not_20_out, not_21_out, not_22_out, or_1_out, or_2_out, or_3_out, or_4_out, or_5_out, or_6_out,
       or_7_out, or_8_out, or_9_out, t_ff_1_q, t_ff_2_q, t_ff_3_q, t_ff_4_q, t_ff_5_q, t_ff_6_q, t_ff_7_q,
       t_ff_8_q, t_ff_9_q, t_ff_10_q, t_ff_11_q, t_ff_12_q, t_ff_13_q, t_ff_14_q, t_ff_15_q, t_ff_16_q,
       t_ff_17_q, t_ff_18_q, t_ff_19_q;

  Clock clock_1 (.out(clock_1_out));
  and and_1 (and_1_out, and_6_out, and_8_out);
  and and_2 (and_2_out, not_22_out, t_ff_6_q, not_1_out, not_2_out);
  and and_3 (and_3_out, and_14_out, and_2_out);
  and and_4 (and_4_out, and_9_out, and_11_out);
  not not_1 (not_1_out, t_ff_1_q);
  T_Flip_Flop #(.trigger("falling")) t_ff_1 (
    .clk(and_13_out), .T(1'b1), .Q(t_ff_1_q), .reset(or_1_out));  // open: Qn, preset, en
  or or_1 (or_1_out, and_3_out, and_5_out);
  and and_5 (and_5_out, not_3_out, t_ff_6_q, not_15_out, t_ff_17_q);
  and and_6 (and_6_out, t_ff_4_q, not_11_out, t_ff_14_q);
  T_Flip_Flop #(.trigger("falling")) t_ff_2 (
    .clk(clock_1_out), .T(1'b1), .Q(t_ff_2_q), .preset(and_1_out), .reset(or_2_out));  // open: Qn, en
  or or_2 (or_2_out, in_8, and_7_out);
  and and_7 (and_7_out, not_4_out, t_ff_7_q, not_16_out, t_ff_18_q);
  and and_8 (and_8_out, not_5_out, not_6_out, not_17_out, t_ff_18_q);
  not not_2 (not_2_out, t_ff_10_q);
  not not_3 (not_3_out, t_ff_1_q);
  and and_9 (and_9_out, t_ff_5_q, not_13_out, t_ff_16_q);
  T_Flip_Flop #(.trigger("falling")) t_ff_3 (
    .clk(and_12_out), .T(1'b1), .Q(t_ff_3_q), .preset(and_4_out), .reset(or_3_out));  // open: Qn, en
  or or_3 (or_3_out, in_5, and_10_out);
  and and_10 (and_10_out, not_7_out, t_ff_8_q, not_20_out, t_ff_19_q);
  and and_11 (and_11_out, not_8_out, not_9_out, not_21_out, t_ff_19_q);
  T_Flip_Flop #(.trigger("falling")) t_ff_4 (
    .clk(and_7_out), .T(1'b1), .Q(t_ff_4_q), .reset(and_12_out));  // open: Qn, preset, en
  and and_12 (and_12_out, not_10_out, t_ff_9_q, t_ff_14_q);
  not not_4 (not_4_out, t_ff_2_q);
  not not_5 (not_5_out, t_ff_2_q);
  not not_6 (not_6_out, t_ff_7_q);
  T_Flip_Flop #(.trigger("falling")) t_ff_5 (
    .clk(and_10_out), .T(1'b1), .Q(t_ff_5_q), .reset(and_13_out));  // open: Qn, preset, en
  and and_13 (and_13_out, not_12_out, t_ff_11_q, t_ff_16_q);
  not not_7 (not_7_out, t_ff_3_q);
  not not_8 (not_8_out, t_ff_3_q);
  not not_9 (not_9_out, t_ff_8_q);
  not not_10 (not_10_out, t_ff_4_q);
  not not_11 (not_11_out, t_ff_9_q);
  and and_14 (and_14_out, not_14_out, not_18_out, t_ff_15_q, not_19_out);
  T_Flip_Flop #(.trigger("falling")) t_ff_6 (
    .clk(and_13_out), .T(t_ff_1_q), .Q(t_ff_6_q), .reset(or_1_out));  // open: Qn, preset, en
  not not_12 (not_12_out, t_ff_5_q);
  not not_13 (not_13_out, t_ff_11_q);
  T_Flip_Flop #(.trigger("falling")) t_ff_7 (
    .clk(clock_1_out), .T(t_ff_2_q), .Q(t_ff_7_q), .reset(or_4_out));  // open: Qn, preset, en
  or or_4 (or_4_out, and_1_out, and_7_out);
  not not_14 (not_14_out, in_1);
  and and_15 (and_15_out, t_ff_1_q, t_ff_6_q);
  T_Flip_Flop #(.trigger("falling")) t_ff_8 (
    .clk(and_12_out), .T(t_ff_3_q), .Q(t_ff_8_q), .reset(or_5_out));  // open: Qn, preset, en
  or or_5 (or_5_out, and_4_out, and_10_out);
  T_Flip_Flop #(.trigger("falling")) t_ff_9 (
    .clk(and_7_out), .T(t_ff_4_q), .Q(t_ff_9_q), .reset(and_12_out));  // open: Qn, preset, en
  and and_16 (and_16_out, t_ff_2_q, t_ff_7_q);
  T_Flip_Flop #(.trigger("falling")) t_ff_10 (
    .clk(and_13_out), .T(and_15_out), .Q(t_ff_10_q), .reset(or_1_out));  // open: Qn, preset, en
  not not_15 (not_15_out, t_ff_10_q);
  T_Flip_Flop #(.trigger("falling")) t_ff_11 (
    .clk(and_10_out), .T(t_ff_5_q), .Q(t_ff_11_q), .reset(and_13_out));  // open: Qn, preset, en
  and and_17 (and_17_out, t_ff_3_q, t_ff_8_q);
  and and_18 (and_18_out, t_ff_4_q, t_ff_9_q);
  T_Flip_Flop #(.trigger("falling")) t_ff_12 (
    .clk(clock_1_out), .T(and_16_out), .Q(t_ff_12_q), .reset(or_6_out));  // open: Qn, preset, en
  or or_6 (or_6_out, and_1_out, and_7_out);
  not not_16 (not_16_out, t_ff_12_q);
  not not_17 (not_17_out, t_ff_12_q);
  not not_18 (not_18_out, in_2);
  not not_19 (not_19_out, in_3);
  and and_19 (and_19_out, and_15_out, t_ff_10_q);
  and and_20 (and_20_out, t_ff_5_q, t_ff_11_q);
  T_Flip_Flop #(.trigger("falling")) t_ff_13 (
    .clk(and_12_out), .T(and_17_out), .Q(t_ff_13_q), .reset(or_7_out));  // open: Qn, preset, en
  or or_7 (or_7_out, and_4_out, and_10_out);
  not not_20 (not_20_out, t_ff_13_q);
  not not_21 (not_21_out, t_ff_13_q);
  T_Flip_Flop #(.trigger("falling")) t_ff_14 (
    .clk(and_7_out), .T(and_18_out), .Q(t_ff_14_q), .reset(and_12_out));  // open: Qn, preset, en
  T_Flip_Flop #(.trigger("falling")) t_ff_15 (
    .clk(and_5_out), .T(1'b1), .Q(t_ff_15_q), .reset(and_3_out));  // open: Qn, preset, en
  not not_22 (not_22_out, t_ff_17_q);
  T_Flip_Flop #(.trigger("falling")) t_ff_16 (
    .clk(and_10_out), .T(and_20_out), .Q(t_ff_16_q), .reset(and_13_out));  // open: Qn, preset, en
  and and_21 (and_21_out, and_17_out, t_ff_13_q);
  and and_22 (and_22_out, and_16_out, t_ff_12_q);
  T_Flip_Flop #(.trigger("falling")) t_ff_17 (
    .clk(and_13_out), .T(and_19_out), .Q(t_ff_17_q), .reset(or_1_out));  // open: Qn, preset, en
  T_Flip_Flop #(.trigger("falling")) t_ff_18 (
    .clk(clock_1_out), .T(and_22_out), .Q(t_ff_18_q), .preset(and_1_out), .reset(or_8_out));  // open: Qn, en
  or or_8 (or_8_out, in_9, and_7_out);
  main main_1 (
    .A(in_1), .B(in_2), .C(in_3), .D(t_ff_15_q), .out_5(main_1_out_5), .out_6(main_1_out_6),
    .out_7(main_1_out_7), .out_8(main_1_out_8), .g(main_1_g), .out_10(main_1_out_10), .out_11(main_1_out_11));
  main main_2 (
    .A(t_ff_17_q), .B(t_ff_10_q), .C(t_ff_6_q), .D(t_ff_1_q), .out_5(main_2_out_5), .out_6(main_2_out_6),
    .out_7(main_2_out_7), .out_8(main_2_out_8), .g(main_2_g), .out_10(main_2_out_10), .out_11(main_2_out_11));
  T_Flip_Flop #(.trigger("falling")) t_ff_19 (
    .clk(and_12_out), .T(and_21_out), .Q(t_ff_19_q), .preset(and_4_out), .reset(or_9_out));  // open: Qn, en
  or or_9 (or_9_out, in_6, and_10_out);
  main main_3 (
    .A(t_ff_19_q), .B(t_ff_13_q), .C(t_ff_8_q), .D(t_ff_3_q), .out_5(main_3_out_5), .out_6(main_3_out_6),
    .out_7(main_3_out_7), .out_8(main_3_out_8), .g(main_3_g), .out_10(main_3_out_10), .out_11(main_3_out_11));
  main main_4 (
    .A(t_ff_18_q), .B(t_ff_12_q), .C(t_ff_7_q), .D(t_ff_2_q), .out_5(main_4_out_5), .out_6(main_4_out_6),
    .out_7(main_4_out_7), .out_8(main_4_out_8), .g(main_4_g), .out_10(main_4_out_10), .out_11(main_4_out_11));
  main main_5 (
    .A(in_4), .B(t_ff_16_q), .C(t_ff_11_q), .D(t_ff_5_q), .out_5(main_5_out_5), .out_6(main_5_out_6),
    .out_7(main_5_out_7), .out_8(main_5_out_8), .g(main_5_g), .out_10(main_5_out_10), .out_11(main_5_out_11));
  main main_6 (
    .A(in_7), .B(t_ff_14_q), .C(t_ff_9_q), .D(t_ff_4_q), .out_5(main_6_out_5), .out_6(main_6_out_6),
    .out_7(main_6_out_7), .out_8(main_6_out_8), .g(main_6_g), .out_10(main_6_out_10), .out_11(main_6_out_11));
  _7_Segment_Display u_7_segment_display_1 (
    .g(main_1_g), .f(main_1_out_8), .a(main_1_out_5), .b(main_1_out_6), .e(main_1_out_10), .d(main_1_out_11),
    .c(main_1_out_7));  // open: dp
  _7_Segment_Display u_7_segment_display_2 (
    .g(main_2_g), .f(main_2_out_8), .a(main_2_out_5), .b(main_2_out_6), .e(main_2_out_10), .d(main_2_out_11),
    .c(main_2_out_7));  // open: dp
  _7_Segment_Display u_7_segment_display_3 (
    .g(main_5_g), .f(main_5_out_8), .a(main_5_out_5), .b(main_5_out_6), .e(main_5_out_10), .d(main_5_out_11),
    .c(main_5_out_7));  // open: dp
  _7_Segment_Display u_7_segment_display_4 (
    .g(main_3_g), .f(main_3_out_8), .a(main_3_out_5), .b(main_3_out_6), .e(main_3_out_10), .d(main_3_out_11),
    .c(main_3_out_7));  // open: dp
  _7_Segment_Display u_7_segment_display_5 (
    .g(main_4_g), .f(main_4_out_8), .a(main_4_out_5), .b(main_4_out_6), .e(main_4_out_10), .d(main_4_out_11),
    .c(main_4_out_7));  // open: dp
  _7_Segment_Display u_7_segment_display_6 (
    .g(main_6_g), .f(main_6_out_8), .a(main_6_out_5), .b(main_6_out_6), .e(main_6_out_10), .d(main_6_out_11),
    .c(main_6_out_7));  // open: dp

  // Notes on the sheet:
  //   Q1
  //   Q1
  //   Q1
  //   Q1
  //   Q1
  //   Q3
  //   Q3
  //   Q4
  //   Q4
  //   Q4
  //   Hour:
  //   Minute:
  //   Second:
endmodule

module bcd_counter (
  input  in_1,
  input  in_2,
  input  in_3
);

  wire main_1_g, main_1_out_5, main_1_out_6, main_1_out_7, main_1_out_8, main_1_out_10, main_1_out_11,
       t_ff_1_q, undriven;

  T_Flip_Flop #(.trigger("falling")) t_ff_1 (.clk(undriven), .T(1'b1), .Q(t_ff_1_q));  // open: Qn, preset, reset, en
  main main_1 (
    .A(in_1), .B(in_2), .C(in_3), .D(t_ff_1_q), .out_5(main_1_out_5), .out_6(main_1_out_6),
    .out_7(main_1_out_7), .out_8(main_1_out_8), .g(main_1_g), .out_10(main_1_out_10), .out_11(main_1_out_11));
  _7_Segment_Display u_7_segment_display_1 (
    .g(main_1_g), .f(main_1_out_8), .a(main_1_out_5), .b(main_1_out_6), .e(main_1_out_10), .d(main_1_out_11),
    .c(main_1_out_7));  // open: dp
endmodule
